// Logisim project Campbell_Reid_Logic_Circuit.circ as structural Verilog: 2 circuits, main circuit part_b
module part_b (
  input  A1,
  input  A2,
  input  A3,
  input  V1,
  input  V2,
  input  V3
);

  wire and_1_out, and_2_out, and_3_out, comparator_1_eq, comparator_2_lt, or_1_out,
       Part_A_successful_acceleration, Test_Acceleration_out;
  wire [2:0] counter_1_q, counter_2_q;

  Button Test_Acceleration (.out(Test_Acceleration_out));
  part_a Part_A (
    .Successful_Acceleration(Part_A_successful_acceleration), .A1(A1), .V1(V1), .A2(A2), .V2(V2), .A3(A3),
    .V3(V3));
  and and_1 (and_1_out, Test_Acceleration_out, ~or_1_out);  // AND_Gate
  LED Successful (.in(Part_A_successful_acceleration));
  and and_2 (and_2_out, and_1_out, Part_A_successful_acceleration);
  and and_3 (and_3_out, ~Part_A_successful_acceleration, and_1_out);  // AND_Gate
  Counter #(.width(3), .max('h7)) counter_1 (.Q(counter_1_q), .clk(and_2_out));  // open: load, D, count, carry, clr
  LED Increase_Success (.in(and_2_out));
  LED Increase_Failure (.in(and_3_out));
  Counter #(.width(3), .max('h7)) counter_2 (.Q(counter_2_q), .clk(and_3_out));  // open: load, D, count, carry, clr
  or or_1 (or_1_out, comparator_2_lt, comparator_1_eq);
  LED Circuit_Locked (.in(comparator_2_lt));
  Comparator #(.width(3), .mode("unsigned")) comparator_1 (
    .a(counter_1_q), .b(3'b111), .eq(comparator_1_eq));  // open: gt, lt
  Comparator #(.width(3), .mode("unsigned")) comparator_2 (
    .a(counter_1_q), .b(counter_2_q), .lt(comparator_2_lt));  // open: gt, eq
endmodule

module part_a (
  input  A1,
  input  A2,
  input  A3,
  input  V1,
  input  V2,
  input  V3,
  output Successful_Acceleration
);

  wire A___1_out, A___2_out, A___3_out, A____1_out, A____2_out, A____3_out, and_1_out, and_2_out, and_3_out,
       and_4_out, and_5_out, and_6_out, and_7_out, and_8_out, and_9_out, and_10_out, and_11_out, and_12_out,
       and_13_out, and_14_out, and_15_out, and_16_out, and_17_out, nor_1_out, nor_2_out, nor_3_out,
       nor_4_out, nor_5_out, not_1_out, not_2_out, not_3_out, not_4_out, not_5_out, not_6_out, not_7_out,
       not_8_out, not_9_out, or_1_out, or_2_out, or_3_out, or_4_out, or_5_out, Turbo_out, V0_S_out, V1_S_out,
       V2_S_out, V3_4_out, V5_S_out, V6_S_out, V7_S_out, V___0_out, V___1_out, V___2_out, V___3_out,
       V___4_out, V___5_out, V___6_out, V___7_out;

  not not_1 (not_1_out, A1);
  not not_2 (not_2_out, A2);
  not not_3 (not_3_out, V2);
  not not_4 (not_4_out, V1);
  and and_1 (and_1_out, A2, A3);
  and and_2 (and_2_out, not_1_out, not_5_out);
  and and_3 (and_3_out, not_1_out, not_2_out);
  and and_4 (and_4_out, not_5_out, not_2_out);
  and and_5 (and_5_out, A3, A1);
  and and_6 (and_6_out, A2, A1);
  and and_7 (and_7_out, A2, A1);
  not not_5 (not_5_out, A3);
  and and_8 (and_8_out, not_3_out, not_4_out);
  and and_9 (and_9_out, not_3_out, not_4_out);
  and and_10 (and_10_out, not_6_out, not_4_out);
  and and_11 (and_11_out, V3, V2);
  and and_12 (and_12_out, not_6_out, not_3_out);
  and and_13 (and_13_out, V3, V1);
  and and_14 (and_14_out, V2, V1);
  and and_15 (and_15_out, V3, V2);
  not not_6 (not_6_out, V3);
  and A____3 (A____3_out, not_1_out, and_1_out);
  and A____2 (A____2_out, A2, and_2_out);
  and A____1 (A____1_out, A3, and_3_out);
  and A___1 (A___1_out, A1, and_4_out);
  and A___2 (A___2_out, not_2_out, and_5_out);
  and A___3 (A___3_out, not_5_out, and_6_out);
  and Turbo (Turbo_out, A3, and_7_out);
  and V___0 (V___0_out, not_6_out, and_8_out);
  and V___1 (V___1_out, V3, and_9_out);
  and V___2 (V___2_out, V2, and_10_out);
  and V___3 (V___3_out, not_4_out, and_11_out);
  and V___4 (V___4_out, V1, and_12_out);
  and V___5 (V___5_out, not_3_out, and_13_out);
  and V___6 (V___6_out, not_6_out, and_14_out);
  and V___7 (V___7_out, V1, and_15_out);
  nor nor_1 (nor_1_out, A____3_out, A____2_out);
  nor nor_2 (nor_2_out, A____1_out, Turbo_out);
  and and_16 (and_16_out, nor_1_out, nor_2_out);
  nor nor_3 (nor_3_out, A____3_out, A____2_out);
  not not_7 (not_7_out, A____3_out);
  not not_8 (not_8_out, A___3_out);
  nor nor_4 (nor_4_out, A___2_out, A___3_out);
  not not_9 (not_9_out, A___1_out);
  nor nor_5 (nor_5_out, A___2_out, A___3_out);
  and and_17 (and_17_out, not_9_out, nor_5_out);
  and V0_S (V0_S_out, and_16_out, V___0_out);
  and V1_S (V1_S_out, nor_3_out, V___1_out);
  and V2_S (V2_S_out, not_7_out, V___2_out);
  or V3_4 (V3_4_out, V___3_out, V___4_out);
  and V5_S (V5_S_out, not_8_out, not_8_out, V___5_out);
  and V6_S (V6_S_out, nor_4_out, V___6_out);
  and V7_S (V7_S_out, and_17_out, V___7_out);
  or or_1 (or_1_out, V0_S_out, V1_S_out);
  or or_2 (or_2_out, V2_S_out, V3_4_out);
  or or_3 (or_3_out, V5_S_out, V6_S_out);
  or or_4 (or_4_out, or_1_out, or_2_out);
  or or_5 (or_5_out, or_3_out, V7_S_out);
  or or_6 (Successful_Acceleration, or_4_out, or_5_out);
endmodule
